# Fritzing sketch energenie breakout board (saved by Fritzing 0.9.1b)
circuit board: 5.64995cm x 6.5005cm
breadboards: 1

parts:
  Raspberry_Pi1 = Raspberry Pi B+
  J1 = double row male pin header, 26 pins [form="♂ (male)"]
  J2 = screw terminal, 3 pins
  J3 = screw terminal, 3 pins
  J4 = double row male pin header, 12 pins [form="♂ (male)"]

nets:
  N1: Raspberry_Pi1.GPIO2, J2.pin1
  N2: Raspberry_Pi1.GPIO3, J3.pin1
  N3: Raspberry_Pi1.GIPO4, J4.pin1
  N4: Raspberry_Pi1.GIPO17, J1.pin6
  N5: Raspberry_Pi1.GIPO27, J1.pin7
  N6: Raspberry_Pi1.GIPO22, J1.pin8
  3.3V: Raspberry_Pi1.3V3, J1.pin9, J2.pin3, J3.pin3, J4.pin9
  N7: Raspberry_Pi1.GIPO10, J4.pin5
  N8: Raspberry_Pi1.GIPO9, J4.pin4
  GND: Raspberry_Pi1.GND, J1.pin24, J2.pin2, J3.pin2, J4.pin10, J4.pin11, J4.pin12
  N9: Raspberry_Pi1.GIPO5, J4.pin2
  N10: Raspberry_Pi1.GIPO6, J4.pin3
  N11: Raspberry_Pi1.GIPO13, J4.pin6
  N12: Raspberry_Pi1.GIPO19, J4.pin7
  N13: Raspberry_Pi1.GIPO26, J4.pin8
  N14: Raspberry_Pi1.GIPO25, J1.pin16
  N15: Raspberry_Pi1.GIPO24, J1.pin18
  N16: Raspberry_Pi1.GIPO23, J1.pin19
  5V: Raspberry_Pi1.5V

notes:
  ENERGENIE BREAKOUT BOARD
  GP13
  GP10
  GP09
  GP06
  GP05
  GP04
  GND
  3V3
  GP26
  GP19
  GP02
  GP03
  V1

custom parts:
  Raspberry Pi B+: The awesome Raspberry Pi ARM Board with 40 pin gipo. Ready for special designed Raspberry Pi B+ Hat (Hardware attached (on) top)
